# Fritzing sketch Schematic (saved by Fritzing 0.9.9b)
breadboards: 1

parts:
  Encoder = YumoE6B2
  Encoder_Button = ENCODER_2LED [package=encoder_led_2]
  Stepper = Stepper Motor - Bipolar
  TB6600_Driver = Pololu A4988 [package=SO16]
  24V = DC Power [voltage=5]
  T-Display = ESP32-TTGO-T-DISPLAY

nets:
  N1: Encoder.V, T-Display.5V
  N2: Encoder.A, T-Display.26
  N3: Encoder.B, T-Display.27
  N4: Encoder.GND, Encoder_Button.-, T-Display.G-1, T-Display.G-10, T-Display.G-11, T-Display.G-14
  N5: Encoder_Button.+G, T-Display.13
  N6: Encoder_Button.+R, T-Display.12
  N7: Encoder_Button.SW, T-Display.15
  N8: Stepper.A, TB6600_Driver.2B
  N9: Stepper.C, TB6600_Driver.2A
  N10: Stepper.B, TB6600_Driver.1A
  N11: Stepper.D, TB6600_Driver.1B
  N12: TB6600_Driver.ENABLE, T-Display.39
  N13: TB6600_Driver.STEP, T-Display.32
  N14: TB6600_Driver.DIR, T-Display.33
  N15: TB6600_Driver.GND, 24V.V-
  N16: TB6600_Driver.VMOT, 24V.V+

custom parts:
  ESP32-TTGO-T-DISPLAY: LILYGO TTGO T-Display GD32VF103CBT6 Main Chip ST7789 1.14 Inch IPS 240x135 Resolution Minimalist Development Board.
